// Logisim project Exercicio06.circ as structural Verilog: 1 circuit, main circuit main
module main (
  input  data_imput,
  input  in_2,
  input  in_3,
  input  in_4,
  input  in_5,
  input  in_6,
  input  in_7,
  input  in_8,
  output data_output,
  output out_10,
  output out_11,
  output out_12,
  output out_13,
  output out_14,
  output out_15,
  output out_16
);

  not not_1 (data_output, data_imput);
  not not_2 (out_10, in_2);
  not not_3 (out_11, in_3);
  not not_4 (out_12, in_4);
  not not_5 (out_13, in_5);
  not not_6 (out_14, in_6);
  not not_7 (out_15, in_7);
  not not_8 (out_16, in_8);
endmodule
