// Logisim project Exercicio02.circ as structural Verilog: 6 circuits, main circuit Exercicio02b
module Exercicio02b (
  input  x,
  input  y,
  input  z,
  output s
);

  wire and_1_out, not_1_out, or_1_out;

  not not_1 (not_1_out, x);
  or or_1 (or_1_out, not_1_out, y);
  and and_1 (and_1_out, y, x);
  or or_2 (s, or_1_out, and_1_out);
endmodule

module Exercicio02c (
  input  x,
  input  y,
  input  z,
  output s
);

  wire and_1_out, not_1_out, not_2_out, not_3_out, or_1_out;

  not not_1 (not_1_out, x);
  not not_2 (not_2_out, y);
  not not_3 (not_3_out, and_1_out);
  and and_1 (and_1_out, not_1_out, y);
  or or_1 (or_1_out, not_2_out, x);
  and and_2 (s, not_3_out, or_1_out);
endmodule

module Exercicio02a (
  input  x,
  input  y,
  input  z,
  output s
);

  wire not_1_out, not_2_out, not_3_out, or_1_out;

  not not_1 (not_1_out, x);
  not not_2 (not_2_out, y);
  or or_1 (or_1_out, not_1_out, not_2_out);
  not not_3 (not_3_out, or_1_out);
  and and_1 (s, x, not_3_out);
endmodule

module Exercicio02d (
  input  x,
  input  y,
  input  z,
  output out_4
);

  wire and_1_out, not_1_out, not_2_out, not_3_out, not_4_out, not_5_out, not_6_out, or_1_out;

  not not_1 (not_1_out, x);
  not not_2 (not_2_out, y);
  not not_3 (not_3_out, x);
  not not_4 (not_4_out, y);
  and and_1 (and_1_out, not_1_out, not_2_out);
  not not_5 (not_5_out, and_1_out);
  or or_1 (or_1_out, not_3_out, not_4_out);
  not not_6 (not_6_out, or_1_out);
  or or_2 (out_4, not_5_out, not_6_out);
endmodule

module Exercicio02e (
  input  x,
  input  y,
  input  z,
  output out_4
);

  wire not_1_out, not_2_out, not_3_out, or_1_out, or_2_out;

  not not_1 (not_1_out, x);
  or or_1 (or_1_out, not_1_out, y);
  or or_2 (or_2_out, x, not_2_out);
  not not_2 (not_2_out, y);
  not not_3 (not_3_out, or_1_out);
  and and_1 (out_4, not_3_out, or_2_out);
endmodule

module main (
  input  in_1,
  input  in_2,
  input  in_3,
  input  in_4,
  input  in_5,
  input  in_6,
  input  in_7,
  input  in_8,
  input  in_9,
  input  in_10,
  input  in_11,
  input  in_12,
  input  in_13,
  input  in_14,
  input  in_15,
  output Exercicio02a,
  output Exercicio02b,
  output Exercicio02c,
  output Exercicio02d,
  output Exercicio02e
);

  Exercicio02a exercicio02a_1 (.x(in_1), .y(in_2), .z(in_3), .s(Exercicio02a));
  Exercicio02b exercicio02b_1 (.x(in_4), .y(in_5), .z(in_6), .s(Exercicio02b));
  Exercicio02c exercicio02c_1 (.x(in_7), .y(in_8), .z(in_9), .s(Exercicio02c));
  Exercicio02d exercicio02d_1 (.x(in_10), .y(in_11), .z(in_12), .out_4(Exercicio02d));
  Exercicio02e exercicio02e_1 (.x(in_13), .y(in_14), .z(in_15), .out_4(Exercicio02e));
endmodule
