// Logisim project Guia05.circ as structural Verilog: 9 circuits, main circuit main
module main (
  input  in_1,
  input  Duvida_2__3_e_7,
  input  Ex1,
  input  Ex5,
  input  in_5,
  input  in_6,
  input  Ex2,
  input  Ex6,
  input  in_9,
  input  in_10,
  input  Ex3,
  input  Ex7,
  input  in_13,
  input  in_14,
  input  Ex4,
  input  Ex8,
  output out_17,
  output out_18,
  output out_19,
  output out_20,
  output out_21,
  output out_22,
  output out_23,
  output out_24,
  output out_25,
  output out_26,
  output out_27,
  output out_28,
  output out_29,
  output out_30,
  output out_31,
  output out_32
);

  Exercicio01 exercicio01_1 (.a(in_1), .b(Ex1), .a_2(in_1), .b_2(Ex1), .out_5(out_17), .Erro(out_19));
  Exercicio02 exercicio02_1 (.a(in_5), .b(Ex2), .a_2(in_5), .b_2(Ex2), .out_5(out_21), .Duvida(out_23));
  Exercicio03 exercicio03_1 (.a(in_9), .b(Ex3), .a_2(in_9), .b_2(Ex3), .out_5(out_25), .Duvida(out_27));
  Exercicio04 exercicio04_1 (.a(in_13), .b(Ex4), .a_2(in_13), .b_2(Ex4), .out_5(out_29), .out_6(out_31));
  Exercicio05 exercicio05_1 (
    .a(Duvida_2__3_e_7), .b(Ex5), .a_2(Duvida_2__3_e_7), .b_2(Ex5), .out_5(out_18), .out_6(out_20));
  Exercicio06 exercicio06_1 (.a(in_6), .b(Ex6), .a_2(in_6), .b_2(Ex6), .out_5(out_22), .out_6(out_24));
  Exercicio06 exercicio06_2 (.a(in_10), .b(Ex7), .a_2(in_10), .b_2(Ex7), .out_5(out_26), .out_6(out_28));
  Exercicio08 exercicio08_1 (.a(in_14), .b(Ex8), .a_2(in_14), .b_2(Ex8), .out_5(out_30), .out_6(out_32));
endmodule

module Exercicio01 (
  input  a,
  input  b,
  input  a_2,
  input  b_2,
  output out_5,
  output Erro
);

  wire not_1_out, not_2_out, or_1_out, or_2_out;

  and and_1 (out_5, a, not_1_out);
  not not_1 (not_1_out, b);
  not not_2 (not_2_out, or_1_out);
  or or_1 (or_1_out, b_2, b_2);
  or or_2 (or_2_out, a_2, not_2_out);
  not not_3 (Erro, or_2_out);
endmodule

module Exercicio02 (
  input  a,
  input  b,
  input  a_2,
  input  b_2,
  output out_5,
  output Duvida
);

  wire and_1_out, and_2_out, not_1_out, not_2_out;

  not not_1 (not_1_out, a);
  or or_1 (out_5, not_1_out, b);
  and and_1 (and_1_out, a_2, a_2);
  not not_2 (not_2_out, and_1_out);
  not not_3 (Duvida, and_2_out);
  and and_2 (and_2_out, not_2_out, b_2);
endmodule

module Exercicio03 (
  input  a,
  input  b,
  input  a_2,
  input  b_2,
  output out_5,
  output Duvida
);

  wire not_1_out, not_2_out, or_2_out, or_3_out;

  not not_1 (not_1_out, a);
  or or_1 (out_5, not_1_out, b);
  not not_2 (not_2_out, or_2_out);
  or or_2 (or_2_out, a_2, a_2);
  or or_3 (or_3_out, not_2_out, b_2);
  not not_3 (Duvida, or_3_out);
endmodule

module Exercicio04 (
  input  a,
  input  b,
  input  a_2,
  input  b_2,
  output out_5,
  output out_6
);

  wire and_1_out, and_2_out, and_3_out, not_1_out, not_3_out;

  not not_1 (not_1_out, b);
  not not_2 (out_5, and_1_out);
  and and_1 (and_1_out, a, not_1_out);
  not not_3 (not_3_out, and_2_out);
  and and_2 (and_2_out, b_2, b_2);
  not not_4 (out_6, and_3_out);
  and and_3 (and_3_out, a_2, not_3_out);
endmodule

module Exercicio05 (
  input  a,
  input  b,
  input  a_2,
  input  b_2,
  output out_5,
  output out_6
);

  wire not_2_out, not_3_out, not_4_out, not_5_out, or_1_out, or_2_out, or_3_out, or_4_out, xor_1_out;

  xor xor_1 (xor_1_out, a, b);
  not not_1 (out_5, xor_1_out);
  or or_1 (or_1_out, a_2, a_2);
  not not_2 (not_2_out, or_1_out);
  not not_3 (not_3_out, or_2_out);
  or or_2 (or_2_out, b_2, b_2);
  not not_4 (not_4_out, or_3_out);
  or or_3 (or_3_out, a_2, b_2);
  or or_4 (or_4_out, not_2_out, not_3_out);
  not not_5 (not_5_out, or_4_out);
  or or_5 (out_6, not_5_out, not_4_out);
endmodule

module Exercicio06 (
  input  a,
  input  b,
  input  a_2,
  input  b_2,
  output out_5,
  output out_6
);

  wire and_1_out, and_2_out, and_3_out, and_4_out, and_5_out, not_1_out, not_2_out, not_3_out, not_4_out;

  xor xor_1 (out_5, a, b);
  and and_1 (and_1_out, a_2, a_2);
  not not_1 (not_1_out, and_1_out);
  and and_2 (and_2_out, b_2, b_2);
  not not_2 (not_2_out, and_2_out);
  not not_3 (not_3_out, and_3_out);
  and and_3 (and_3_out, not_1_out, b_2);
  not not_4 (not_4_out, and_4_out);
  and and_4 (and_4_out, not_2_out, a_2);
  and and_5 (and_5_out, not_3_out, not_4_out);
  not not_5 (out_6, and_5_out);
endmodule

module Exercicio07 (
  input  a,
  input  b,
  input  a_2,
  input  b_2,
  output out_5,
  output Duvida
);

  wire not_1_out, not_2_out, not_4_out, not_5_out, or_1_out, or_2_out, xor_1_out;

  not not_1 (not_1_out, a);
  not not_2 (not_2_out, b);
  xor xor_1 (xor_1_out, not_1_out, not_2_out);
  not not_3 (out_5, xor_1_out);
  not not_4 (not_4_out, or_1_out);
  or or_1 (or_1_out, a_2, a_2);
  or or_2 (or_2_out, b_2, b_2);
  not not_5 (not_5_out, or_2_out);
  or or_3 (Duvida, not_4_out, not_5_out);
endmodule

module Exercicio08 (
  input  a,
  input  b,
  input  a_2,
  input  b_2,
  output out_5,
  output out_6
);

  wire and_1_out, and_2_out, and_3_out, and_4_out, not_1_out, not_3_out, not_4_out, not_5_out;

  not not_1 (not_1_out, a);
  not not_2 (out_5, and_1_out);
  and and_1 (and_1_out, not_1_out, not_3_out);
  not not_3 (not_3_out, b);
  not not_4 (not_4_out, and_2_out);
  and and_2 (and_2_out, a_2, a_2);
  not not_5 (not_5_out, and_3_out);
  and and_3 (and_3_out, b_2, b_2);
  and and_4 (and_4_out, not_4_out, not_5_out);
  not not_6 (out_6, and_4_out);
endmodule
