// Logisim project Guia06.circ as structural Verilog: 8 circuits, main circuit Questão1
module \Questão1  (
  input  x,
  input  y,
  input  z,
  output out_4,
  output out_5,
  output out_6,
  output out_7,
  output out_8
);

  wire and_1_out, and_2_out, and_3_out, and_4_out, and_5_out, and_6_out, and_7_out, and_8_out, not_1_out,
       not_2_out, not_3_out, not_4_out, not_5_out, not_6_out, not_7_out, not_8_out;

  not not_1 (not_1_out, y);
  and and_1 (and_1_out, not_1_out, z);
  and and_2 (and_2_out, x, z);
  not not_2 (not_2_out, y);
  and and_3 (and_3_out, not_2_out, not_3_out);
  not not_3 (not_3_out, z);
  and and_4 (and_4_out, x, not_4_out);
  not not_4 (not_4_out, z);
  not not_5 (not_5_out, x);
  and and_5 (and_5_out, not_5_out, z);
  and and_6 (and_6_out, y, not_6_out);
  not not_6 (not_6_out, z);
  not not_7 (not_7_out, y);
  and and_7 (and_7_out, not_7_out, not_8_out);
  not not_8 (not_8_out, z);
  and and_8 (and_8_out, x, y);
  or or_1 (out_4, and_1_out, and_2_out);
  or or_2 (out_5, and_3_out, and_4_out);
  or or_3 (out_7, and_5_out, and_6_out);
  or or_4 (out_8, and_7_out, and_8_out);

  assign out_6 = y;

  // Notes on the sheet:
  //   A)
  //   B)
  //   C)
  //   D)
  //   E)
endmodule

module \Questão2  (
  input  X,
  input  Y,
  input  Z,
  output out_4,
  output out_5,
  output out_6,
  output out_7,
  output out_8
);

  wire not_1_out, not_2_out, not_3_out, not_4_out, not_5_out, not_6_out, not_7_out, not_8_out, not_9_out,
       not_10_out, not_11_out, not_12_out, not_13_out, or_1_out, or_2_out, or_3_out, or_4_out, or_5_out,
       or_6_out, or_7_out, or_8_out, or_9_out, or_10_out;

  not not_1 (not_1_out, X);
  not not_2 (not_2_out, Z);
  not not_3 (not_3_out, Y);
  not not_4 (not_4_out, Z);
  not not_5 (not_5_out, Y);
  not not_6 (not_6_out, X);
  not not_7 (not_7_out, Y);
  not not_8 (not_8_out, Z);
  not not_9 (not_9_out, X);
  not not_10 (not_10_out, X);
  not not_11 (not_11_out, Z);
  not not_12 (not_12_out, Y);
  not not_13 (not_13_out, Y);
  or or_1 (or_1_out, not_1_out, not_2_out);
  and and_1 (out_4, or_1_out, or_2_out);
  or or_2 (or_2_out, not_3_out, not_4_out);
  or or_3 (or_3_out, not_5_out, Z);
  and and_2 (out_5, or_3_out, or_4_out);
  or or_4 (or_4_out, not_6_out, Z);
  or or_5 (or_5_out, X, not_7_out, Z);
  or or_6 (or_6_out, Y, not_8_out);
  and and_3 (out_6, or_5_out, or_6_out, or_7_out);
  or or_7 (or_7_out, not_9_out, Y);
  not not_14 (out_7, Y);
  or or_8 (or_8_out, not_10_out, Y, not_11_out);
  and and_4 (out_8, or_8_out, or_9_out, or_10_out);
  or or_9 (or_9_out, X, not_12_out);
  or or_10 (or_10_out, not_13_out, Z);

  // Notes on the sheet:
  //   A)
  //   B)
  //   C)
  //   D)
  //   E)
endmodule

module \Questão3  (
  input  x,
  input  y,
  input  z,
  input  w,
  output out_5,
  output out_6,
  output out_7,
  output out_8,
  output out_9
);

  wire and_1_out, and_2_out, and_3_out, and_4_out, and_5_out, and_6_out, and_7_out, and_8_out, and_9_out,
       and_10_out, and_11_out, and_12_out, and_13_out, and_14_out, and_15_out, and_16_out, and_17_out,
       and_18_out, and_19_out, and_20_out, and_21_out, and_22_out, not_1_out, not_2_out, not_3_out,
       not_4_out, not_5_out, not_6_out, not_7_out, not_8_out, not_9_out, not_10_out, not_11_out, not_12_out,
       not_13_out, not_14_out, not_15_out, not_16_out, not_17_out, not_18_out, not_19_out, not_20_out,
       not_21_out, not_22_out, not_23_out, not_24_out, not_25_out, not_26_out, not_27_out, not_28_out,
       not_29_out, not_30_out, not_31_out, not_32_out, not_33_out, not_34_out, not_35_out;

  not not_1 (not_1_out, x);
  not not_2 (not_2_out, z);
  and and_1 (and_1_out, not_1_out, not_2_out, w);
  and and_2 (and_2_out, x, not_3_out, w);
  not not_3 (not_3_out, z);
  and and_3 (and_3_out, x, not_4_out, w);
  not not_4 (not_4_out, y);
  not not_5 (not_5_out, x);
  not not_6 (not_6_out, y);
  and and_4 (and_4_out, not_5_out, not_6_out, z, not_7_out);
  not not_7 (not_7_out, w);
  not not_8 (not_8_out, x);
  and and_5 (and_5_out, not_8_out, not_9_out, not_10_out);
  not not_9 (not_9_out, y);
  not not_10 (not_10_out, z);
  not not_11 (not_11_out, x);
  and and_6 (and_6_out, not_11_out, not_12_out, w);
  not not_12 (not_12_out, z);
  not not_13 (not_13_out, x);
  and and_7 (and_7_out, not_13_out, z, w);
  and and_8 (and_8_out, x, z, w);
  not not_14 (not_14_out, x);
  not not_15 (not_15_out, y);
  and and_9 (and_9_out, not_14_out, not_15_out, not_16_out);
  not not_16 (not_16_out, z);
  and and_10 (and_10_out, x, not_17_out, w);
  not not_17 (not_17_out, z);
  not not_18 (not_18_out, x);
  and and_11 (and_11_out, not_18_out, z, not_19_out);
  not not_19 (not_19_out, w);
  not not_20 (not_20_out, x);
  and and_12 (and_12_out, not_20_out, y, z);
  and and_13 (and_13_out, y, z, not_21_out);
  not not_21 (not_21_out, w);
  not not_22 (not_22_out, x);
  and and_14 (and_14_out, not_22_out, y, not_23_out);
  not not_23 (not_23_out, w);
  not not_24 (not_24_out, x);
  and and_15 (and_15_out, not_24_out, z, not_25_out);
  not not_25 (not_25_out, w);
  not not_26 (not_26_out, x);
  and and_16 (and_16_out, not_26_out, y, z);
  and and_17 (and_17_out, y, z, not_27_out);
  not not_27 (not_27_out, w);
  not not_28 (not_28_out, z);
  and and_18 (and_18_out, x, not_28_out, w);
  not not_29 (not_29_out, x);
  not not_30 (not_30_out, y);
  and and_19 (and_19_out, not_29_out, not_30_out, not_31_out);
  not not_31 (not_31_out, z);
  not not_32 (not_32_out, x);
  and and_20 (and_20_out, not_32_out, y, w);
  and and_21 (and_21_out, x, not_33_out, not_34_out);
  not not_33 (not_33_out, z);
  not not_34 (not_34_out, w);
  not not_35 (not_35_out, z);
  and and_22 (and_22_out, x, not_35_out, w);
  or or_1 (out_5, and_1_out, and_2_out, and_3_out, and_4_out);
  or or_2 (out_6, and_5_out, and_6_out, and_7_out, and_8_out);
  or or_3 (out_7, and_9_out, and_10_out, and_11_out, and_12_out, and_13_out);
  or or_4 (out_8, and_14_out, and_15_out, and_16_out, and_17_out, and_18_out);
  or or_5 (out_9, and_19_out, and_20_out, and_21_out, and_22_out);

  // Notes on the sheet:
  //   A)
  //   B)
  //   C)
  //   D)
  //   E)
endmodule

module \Questão4  (
  input  X,
  input  Y,
  input  Z,
  input  W,
  output out_5,
  output out_6,
  output out_7,
  output out_8,
  output out_9
);

  wire not_1_out, not_2_out, not_3_out, not_4_out, not_5_out, not_6_out, not_7_out, not_8_out, not_9_out,
       not_10_out, not_11_out, not_12_out, not_13_out, not_14_out, not_15_out, not_16_out, not_17_out,
       not_18_out, not_19_out, not_20_out, not_21_out, not_22_out, not_23_out, not_24_out, not_25_out,
       not_26_out, not_27_out, not_28_out, not_29_out, not_30_out, not_31_out, not_32_out, not_33_out,
       or_1_out, or_2_out, or_3_out, or_4_out, or_5_out, or_6_out, or_7_out, or_8_out, or_9_out, or_10_out,
       or_11_out, or_12_out, or_13_out, or_14_out, or_15_out, or_16_out, or_17_out;

  or or_1 (or_1_out, X, Y, not_1_out, W);
  not not_1 (not_1_out, Z);
  not not_2 (not_2_out, Y);
  or or_2 (or_2_out, not_2_out, Z, not_3_out);
  not not_3 (not_3_out, W);
  or or_3 (or_3_out, X, not_4_out, not_5_out);
  not not_4 (not_4_out, Y);
  not not_5 (not_5_out, W);
  not not_6 (not_6_out, Y);
  not not_7 (not_7_out, Z);
  or or_4 (or_4_out, not_6_out, not_7_out, W);
  not not_8 (not_8_out, Y);
  or or_5 (or_5_out, X, not_8_out, W);
  not not_9 (not_9_out, X);
  or or_6 (or_6_out, not_9_out, Y, not_10_out);
  not not_10 (not_10_out, W);
  not not_11 (not_11_out, Y);
  or or_7 (or_7_out, X, not_11_out, Z, W);
  not not_12 (not_12_out, X);
  not not_13 (not_13_out, Y);
  or or_8 (or_8_out, not_12_out, not_13_out, not_14_out);
  not not_14 (not_14_out, W);
  not not_15 (not_15_out, X);
  or or_9 (or_9_out, not_15_out, Y, Z);
  or or_10 (or_10_out, X, Z, not_16_out);
  not not_16 (not_16_out, W);
  not not_17 (not_17_out, Y);
  or or_11 (or_11_out, X, not_17_out, not_18_out);
  not not_18 (not_18_out, W);
  not not_19 (not_19_out, X);
  or or_12 (or_12_out, not_19_out, not_20_out, not_21_out);
  not not_20 (not_20_out, Y);
  not not_21 (not_21_out, W);
  not not_22 (not_22_out, X);
  not not_23 (not_23_out, Y);
  or or_13 (or_13_out, not_22_out, not_23_out, not_24_out);
  not not_24 (not_24_out, Z);
  or or_14 (or_14_out, X, not_25_out, not_26_out);
  not not_25 (not_25_out, Z);
  not not_26 (not_26_out, W);
  or or_15 (or_15_out, X, not_27_out, not_28_out);
  not not_27 (not_27_out, Y);
  not not_28 (not_28_out, W);
  not not_29 (not_29_out, X);
  or or_16 (or_16_out, not_29_out, not_30_out, not_31_out);
  not not_30 (not_30_out, Y);
  not not_31 (not_31_out, W);
  not not_32 (not_32_out, Y);
  not not_33 (not_33_out, Z);
  or or_17 (or_17_out, not_32_out, not_33_out, W);
  and and_1 (out_5, or_1_out, or_2_out, or_3_out);
  and and_2 (out_6, or_4_out, or_5_out, or_6_out);
  and and_3 (out_7, or_7_out, or_8_out, or_9_out);
  and and_4 (out_8, or_10_out, or_11_out, or_12_out, or_13_out);
  and and_5 (out_9, or_14_out, or_15_out, or_16_out, or_17_out);

  // Notes on the sheet:
  //   A)
  //   B)
  //   C)
  //   D)
  //   E)
endmodule

module \Questão5  (
  input  x,
  input  y,
  input  z,
  output out_4,
  output out_5
);

  wire and_1_out, and_2_out, and_3_out, and_4_out, and_5_out, not_1_out, not_2_out, not_3_out, not_4_out,
       not_5_out, not_6_out, not_7_out, not_8_out, or_1_out, or_2_out;

  not not_1 (not_1_out, x);
  not not_2 (not_2_out, y);
  not not_3 (not_3_out, y);
  not not_4 (not_4_out, z);
  or or_1 (or_1_out, not_1_out, not_2_out);
  not not_5 (not_5_out, or_1_out);
  and and_1 (and_1_out, not_5_out, not_6_out);
  and and_2 (and_2_out, x, y);
  not not_6 (not_6_out, and_2_out);
  and and_3 (and_3_out, y, z);
  or or_2 (or_2_out, and_3_out, not_8_out);
  not not_7 (not_7_out, or_2_out);
  not not_8 (not_8_out, x);
  and and_4 (and_4_out, x, not_3_out);
  or or_3 (out_5, and_4_out, and_5_out);
  and and_5 (and_5_out, x, not_4_out);
  or or_4 (out_4, and_1_out, not_7_out);
endmodule

module \Questão6  (
  input  X,
  input  Y,
  input  W,
  input  Z,
  output S,
  output S_2
);

  wire and_1_out, and_2_out, and_3_out, not_1_out, not_2_out, not_3_out, not_4_out, not_5_out, not_6_out,
       not_7_out, not_8_out, not_9_out, not_10_out, not_11_out, not_12_out, not_13_out, not_14_out, or_1_out,
       or_2_out, or_3_out, or_4_out, or_5_out, or_6_out, or_7_out;

  not not_1 (not_1_out, X);
  or or_1 (or_1_out, not_1_out, not_2_out, W);
  not not_2 (not_2_out, Y);
  and and_1 (and_1_out, X, Y, not_3_out);
  not not_3 (not_3_out, W);
  and and_2 (and_2_out, Y, W, Z);
  or or_2 (or_2_out, X, Y, W);
  or or_3 (or_3_out, X, Y, not_4_out);
  not not_4 (not_4_out, W);
  not not_5 (not_5_out, Y);
  or or_4 (or_4_out, X, not_5_out, W);
  not not_6 (not_6_out, Y);
  or or_5 (or_5_out, X, not_6_out, not_7_out);
  not not_7 (not_7_out, W);
  not not_8 (not_8_out, Y);
  or or_6 (or_6_out, not_8_out, not_9_out, not_10_out);
  not not_9 (not_9_out, W);
  not not_10 (not_10_out, Z);
  not not_11 (not_11_out, or_1_out);
  and and_3 (and_3_out, not_11_out, not_12_out);
  not not_12 (not_12_out, and_1_out);
  or or_7 (or_7_out, and_2_out, not_14_out);
  not not_13 (not_13_out, or_7_out);
  not not_14 (not_14_out, X);
  and and_4 (S_2, or_2_out, or_3_out, or_4_out, or_5_out, or_6_out);
  or or_8 (S, and_3_out, not_13_out);
endmodule

module \Questão7  (
  input  X,
  input  Y,
  input  Z,
  output S,
  output S_2
);

  wire not_1_out, not_2_out, not_3_out, not_4_out, not_5_out, not_6_out, or_1_out, or_2_out, or_3_out,
       or_4_out, or_5_out;

  not not_1 (not_1_out, Y);
  not not_2 (not_2_out, Z);
  not not_3 (not_3_out, X);
  not not_4 (not_4_out, Y);
  not not_5 (not_5_out, X);
  not not_6 (not_6_out, Y);
  or or_1 (or_1_out, X, not_1_out, not_2_out);
  or or_2 (or_2_out, not_3_out, Y, Z);
  or or_3 (or_3_out, X, not_4_out, Z);
  or or_4 (or_4_out, not_5_out, Y, Z);
  and and_1 (S_2, or_4_out, or_5_out);
  or or_5 (or_5_out, X, not_6_out);
  and and_2 (S, or_1_out, or_2_out, or_3_out);
endmodule

module \Questão8  (
  input  w,
  input  x,
  input  y,
  input  z,
  output out_5
);

  wire and_1_out, and_2_out, and_3_out, and_4_out, not_1_out, not_2_out, not_3_out, not_4_out, not_5_out,
       not_6_out, not_7_out;

  and and_1 (and_1_out, w, x, y, z);
  and and_2 (and_2_out, w, x, not_1_out, not_2_out);
  not not_1 (not_1_out, y);
  not not_2 (not_2_out, z);
  not not_3 (not_3_out, x);
  and and_3 (and_3_out, w, not_3_out, not_4_out, z);
  not not_4 (not_4_out, y);
  not not_5 (not_5_out, w);
  not not_6 (not_6_out, x);
  and and_4 (and_4_out, not_5_out, not_6_out, y, not_7_out);
  not not_7 (not_7_out, z);
  or or_1 (out_5, and_1_out, and_2_out, and_3_out, and_4_out);

  // Notes on the sheet:
  //   Não há simplificação
endmodule
