// Logisim project HalfAdder_FullAdder.circ as structural Verilog: 3 circuits, main circuit Sum_Of_4_Bits
module Sum_Of_4_Bits (
  input  A3,
  input  A2,
  input  A1,
  input  A0,
  input  B3,
  input  B2,
  input  B1,
  input  B0,
  output S4,
  output S3,
  output S2,
  output S1,
  output S0
);

  wire fulladder_2_vai1, fulladder_3_vai1, halfadder_1_v1;

  fullAdder fulladder_1 (.A(A3), .B(B3), .S(S3), .Vai1(S4), .Vem1(fulladder_2_vai1));
  fullAdder fulladder_2 (.A(A2), .B(B2), .S(S2), .Vai1(fulladder_2_vai1), .Vem1(fulladder_3_vai1));
  halfAdder halfadder_1 (.A(A0), .B(B0), .S(S0), .V1(halfadder_1_v1));
  fullAdder fulladder_3 (.A(A1), .B(B1), .S(S1), .Vai1(fulladder_3_vai1), .Vem1(halfadder_1_v1));
endmodule

module halfAdder (
  input  A,
  input  B,
  output S,
  output V1
);

  xor xor_1 (S, A, B);
  and and_1 (V1, A, B);
endmodule

module fullAdder (
  input  Vem1,
  input  A,
  input  B,
  output S,
  output Vai1
);

  wire and_1_out, and_2_out, and_3_out, and_4_out, and_5_out, and_6_out, and_7_out, not_1_out, not_2_out,
       not_3_out;

  not not_1 (not_1_out, A);
  not not_2 (not_2_out, B);
  not not_3 (not_3_out, Vem1);
  and and_1 (and_1_out, not_1_out, not_2_out, Vem1);
  and and_2 (and_2_out, not_1_out, B, not_3_out);
  and and_3 (and_3_out, A, not_2_out, not_3_out);
  and and_4 (and_4_out, A, B, Vem1);
  and and_5 (and_5_out, A, Vem1);
  and and_6 (and_6_out, B, Vem1);
  and and_7 (and_7_out, A, B);
  or or_1 (S, and_1_out, and_2_out, and_3_out, and_4_out);
  or or_2 (Vai1, and_5_out, and_6_out, and_7_out);

  // Notes on the sheet:
  //   A
  //   B
  //   V
endmodule
