// Logisim project MUX_DMUX.circ as structural Verilog: 1 circuit, main circuit main
module main (
  input  E0,
  input  E,
  input  E1,
  input  C,
  input  C_2,
  input  E0_2,
  input  E1_2,
  input  E_2,
  input  E2,
  input  E3,
  input  C1,
  input  C2,
  input  C1_2,
  input  C2_2,
  output S0,
  output S,
  output S1,
  output S0_2,
  output S1_2,
  output S_2,
  output S2,
  output S3
);

  wire and_1_out, and_2_out, and_3_out, and_4_out, and_5_out, and_6_out, not_1_out, not_2_out, not_3_out,
       not_4_out, not_5_out, not_6_out, not_7_out, not_8_out, not_9_out, not_10_out;

  and and_1 (and_1_out, E0, not_1_out);
  not not_1 (not_1_out, C_2);
  and and_2 (and_2_out, E1, C_2);
  and and_3 (and_3_out, E0_2, not_2_out, not_3_out);
  not not_2 (not_2_out, C1);
  not not_3 (not_3_out, C2);
  not not_4 (not_4_out, C1);
  and and_4 (and_4_out, E1_2, not_4_out, C2);
  and and_5 (and_5_out, E2, C1, not_5_out);
  not not_5 (not_5_out, C2);
  and and_6 (and_6_out, E3, C1, C2);
  or or_1 (S, and_1_out, and_2_out);
  or or_2 (S_2, and_3_out, and_4_out, and_5_out, and_6_out);
  not not_6 (not_6_out, C);
  and and_7 (S0, not_6_out, E);
  and and_8 (S1, E, C);
  and and_9 (S0_2, E_2, not_7_out, not_8_out);
  not not_7 (not_7_out, C1_2);
  not not_8 (not_8_out, C2_2);
  not not_9 (not_9_out, C1_2);
  and and_10 (S1_2, E_2, not_9_out, C2_2);
  and and_11 (S2, E_2, C1_2, not_10_out);
  not not_10 (not_10_out, C2_2);
  and and_12 (S3, E_2, C1_2, C2_2);

  // Notes on the sheet:
  //   MUX
  //   E = 2C
  //   E0 | E1 | A   A' |$0   | 0   | 0   1  |$0   | 1   | 0   1  |$1   | 0   | 1   0  |$1   | 1   | 1   0  |
endmodule
